# Fritzing sketch Gripper_schematic (saved by Fritzing 0.9.2b)
breadboards: 1

parts:
  U1 = MAX485 [package=dil08]
  part = Arduino Micro (Rev3) [part_number=1]
  J2 = male pin header, 2 pins [form="♂ (male)"]
  Q1 = MOSFET-NCHANNEL [package=dpak]
  R1 = Resistor [tolerance=±10% resistance=10k package=THT]
  J3 = rounded female pin header, 2 pins [form="♀ (female rounded)"]
  J3_2 = rounded female pin header, 2 pins [form="♀ (female rounded)"]  # not connected

nets:
  N1: U1.RO, part.D0/RX
  N2: U1.RE, part.D8_PWM/A8
  N3: U1.DE, part.D9_PWM/A9
  N4: U1.DI, part.D1/TX
  GND: U1.GND, part.GND, Q1.S, R1.Pin_1
  N5: U1.A, J2.pin1
  N6: U1.B, J2.pin2
  5V: U1.VCC, part.5V
  N7: part.RESET, part.D12_PWM/A11
  N8: part.D10_PWM/A10, Q1.G
  N9: Q1.D, J3.pin2
  12V: J3.pin1
